// Logisim project 2주차_1_(2)번_예시답안.circ as structural Verilog: 1 circuit, main circuit main
module main (
  input  A,
  input  B,
  output Y
);

  wire not_1_out;

  not not_1 (not_1_out, B);
  and and_1 (Y, A, not_1_out);
endmodule
