// Logisim project 2주차_2번_예시답안.circ as structural Verilog: 1 circuit, main circuit main
module main (
  input  A,
  input  B,
  input  C,
  input  A_2,
  input  B_2,
  output Y,
  output Y_2
);

  wire and_1_out, and_2_out, and_3_out, and_5_out, not_1_out, not_2_out, not_3_out;

  not not_1 (not_1_out, A);
  not not_2 (not_2_out, A_2);
  and and_1 (and_1_out, not_1_out, B);
  not not_3 (not_3_out, C);
  and and_2 (and_2_out, not_1_out, B);
  and and_3 (and_3_out, and_2_out, C);
  and and_4 (Y_2, not_2_out, B_2);
  and and_5 (and_5_out, and_1_out, not_3_out);
  or or_1 (Y, and_5_out, and_3_out);
endmodule
