// Logisim project 3주차_2번문제.circ as structural Verilog: 1 circuit, main circuit main
module main (
  input  A,
  input  B,
  input  C,
  output out_4,
  output out_5,
  output out_6,
  output out_7,
  output out_8,
  output out_9,
  output out_10,
  output out_11
);

  wire and_1_out, and_2_out, and_3_out, and_4_out, and_5_out, and_6_out, and_7_out, and_8_out, not_1_out,
       not_2_out, not_3_out;

  not not_1 (not_1_out, A);
  not not_2 (not_2_out, B);
  not not_3 (not_3_out, C);
  and and_1 (and_1_out, not_1_out, not_2_out);
  and and_2 (and_2_out, not_1_out, not_2_out);
  and and_3 (and_3_out, not_1_out, B);
  and and_4 (and_4_out, not_1_out, B);
  and and_5 (and_5_out, A, not_2_out);
  and and_6 (and_6_out, A, not_2_out);
  and and_7 (and_7_out, A, B);
  and and_8 (and_8_out, B, A);
  and and_9 (out_4, and_1_out, not_3_out);
  and and_10 (out_5, and_2_out, C);
  and and_11 (out_6, and_3_out, not_3_out);
  and and_12 (out_7, and_4_out, C);
  and and_13 (out_8, and_5_out, not_3_out);
  and and_14 (out_9, and_6_out, C);
  and and_15 (out_10, and_7_out, not_3_out);
  and and_16 (out_11, and_8_out, C);
endmodule
