// Logisim project 4주차_1번_모범답안.circ as structural Verilog: 1 circuit, main circuit main
module main (
  input  En,
  input  S1,
  input  S0,
  input  S1_2,
  input  S0_2,
  output Y1,
  output Y2,
  output Y3,
  output Y4,
  output V
);

  wire and_1_out, and_2_out, and_3_out, and_4_out, and_9_out, and_10_out, and_11_out, and_12_out, and_13_out,
       and_14_out, and_15_out, and_16_out, not_1_out, not_2_out, not_3_out, not_4_out, or_1_out, or_3_out;

  not not_1 (not_1_out, S0);
  not not_2 (not_2_out, S1);
  and and_1 (and_1_out, not_1_out, not_2_out);
  and and_2 (and_2_out, S0, not_2_out);
  and and_3 (and_3_out, not_1_out, S1);
  and and_4 (and_4_out, S0, S1);
  and and_5 (Y1, and_1_out, En);
  and and_6 (Y2, and_2_out, En);
  and and_7 (Y3, and_3_out, En);
  and and_8 (Y4, and_4_out, En);
  not not_3 (not_3_out, S0_2);
  not not_4 (not_4_out, S1_2);
  and and_9 (and_9_out, Y1, not_3_out);
  and and_10 (and_10_out, and_9_out, not_4_out);
  and and_11 (and_11_out, Y2, S0_2);
  and and_12 (and_12_out, Y3, not_3_out);
  and and_13 (and_13_out, Y4, S0_2);
  and and_14 (and_14_out, and_11_out, not_4_out);
  and and_15 (and_15_out, and_12_out, S1_2);
  and and_16 (and_16_out, and_13_out, S1_2);
  or or_1 (or_1_out, and_10_out, and_14_out);
  or or_2 (V, or_1_out, or_3_out);
  or or_3 (or_3_out, and_15_out, and_16_out);
endmodule
