// Logisim project 4주차_2번_모범답안.circ as structural Verilog: 1 circuit, main circuit main
module main (
  input  D,
  output Q,
  output Q_prime
);

  wire CLK_out, nand_1_out, nand_2_out, nand_3_out, nand_4_out, nand_5_out, nand_6_out, not_1_out;

  Clock CLK (.out(CLK_out));
  not not_1 (not_1_out, CLK_out);
  nand nand_1 (nand_1_out, D, not_1_out);
  nand nand_2 (nand_2_out, not_1_out, ~D);  // NAND_Gate
  nand nand_3 (nand_3_out, nand_1_out, nand_4_out);
  nand nand_4 (nand_4_out, nand_3_out, nand_2_out);
  nand nand_5 (nand_5_out, nand_3_out, CLK_out);
  nand nand_6 (nand_6_out, CLK_out, ~nand_3_out);  // NAND_Gate
  nand nand_7 (Q, nand_5_out, Q_prime);
  nand nand_8 (Q_prime, Q, nand_6_out);
endmodule
